# Fritzing sketch EncenderYApagarLed (saved by Fritzing 0.9.3b)
breadboards: 1

parts:
  Part1 = SparkFun ESP8266 Thing
  LED1 = smd LED [color="Blue (525nm)" package="0805 [SMD]"]
  R1 = Resistor [tolerance=±5% resistance=330 package="0402 [SMD]"]

nets:
  N1: Part1.GND, R1.Pin_1
  N2: Part1.GPIO4, LED1.anode
  N3: LED1.cathode, R1.Pin_0
