# Fritzing sketch Push_Button_y_LED (saved by Fritzing 0.9.3b)
breadboards: 1

parts:
  R1 = Resistor [tolerance=±5% resistance=330 package="0402 [SMD]"]
  LED1 = smd LED [color="Blue (525nm)" package="0805 [SMD]"]
  R2 = Resistor [tolerance=±5% resistance=10k package=THT]
  S1 = Pushbutton [package="[THT]"]
  Part1 = SparkFun ESP8266 Thing

nets:
  N1: R1.Pin_0, LED1.cathode
  N2: R1.Pin_1, S1.Pin_3, S1.Pin_4, Part1.GND
  N3: LED1.anode, Part1.GPIO4
  N4: R2.Pin_0, S1.Pin_1, S1.Pin_2, Part1.GPIO5
  N5: R2.Pin_1, Part1.VCC
