# Fritzing sketch Escritura_Serial (saved by Fritzing 0.9.3b)
breadboards: 1

parts:
  Part1 = SparkFun ESP8266 Thing
  R1 = Rotary Potentiometer (Small) [maximum_resistance=100kΩ package=THT]

nets:
  N1: Part1.GND, R1.leg1
  N2: Part1.VCC, R1.leg2
  N3: Part1.ADC, R1.wiper
