# Fritzing sketch ADC_Potenciometro (saved by Fritzing 0.9.3b)
breadboards: 1

parts:
  Part1 = SparkFun ESP8266 Thing
  R1 = Rotary Potentiometer (Small) [maximum_resistance=100kΩ package=THT]
  LED1 = LED - 5mm [color="Green (565nm)" package="5 mm [THT]"]
  R2 = Resistor [tolerance=±5% resistance=330 package=THT]

nets:
  N1: Part1.GND, R1.leg1
  N2: Part1.VCC, R1.leg2, R2.Pin_1
  N3: Part1.GPIO4, LED1.cathode
  N4: Part1.ADC, R1.wiper
  N5: LED1.anode, R2.Pin_0
