# Fritzing sketch Fotoresistencia (saved by Fritzing 0.9.3b)
breadboards: 1

parts:
  Part1 = SparkFun ESP8266 Thing
  R1 = Photocell (LDR) [package=THT]
  R2 = Resistor [tolerance=±5% resistance=330 package=THT]
  LED1 = LED - 5mm [color="Green (570nm)" package="5 mm [THT]"]
  R3 = Resistor [tolerance=±5% resistance=220 package=THT]

nets:
  N1: Part1.GND, R2.Pin_0
  N2: Part1.VCC, R1.pin_1, R3.Pin_1
  N3: Part1.GPIO2, LED1.cathode
  N4: Part1.ADC, R1.pin_0, R2.Pin_1
  N5: LED1.anode, R3.Pin_0
