# Fritzing sketch Sensor_Distancia (saved by Fritzing 0.9.3b)
breadboards: 1

parts:
  hc-sr1 = hc-sr04 [part_number=hcsr04]
  U1 = NodeMCU V1.0

nets:
  VCC: hc-sr1.VCC, U1.Vin
  N1: hc-sr1.Trig, U1.D1
  N2: hc-sr1.Echo, U1.D2
  GND: hc-sr1.GND, U1.GND

custom parts:
  hc-sr04: This is a HC-SR04 Distance Sensor
  NodeMCU V1.0: ESP8266 based NodeMCU
