# Fritzing sketch Motor_DC (saved by Fritzing 0.9.3b)
breadboards: 1

parts:
  Part1 = SparkFun ESP8266 Thing
  Part2 = Motor Driver 1A Dual TB6612FNG
  M1 = DC Motor
  R1 = Rotary Potentiometer (Small) [maximum_resistance=100kΩ package=THT]
  S1 = Pushbutton [package="[THT]"]

nets:
  GND: Part1.GND, Part2.GND, R1.leg1, S1.Pin_1, S1.Pin_2
  VCC: Part1.VCC, Part2.VCC, Part2.STBY, R1.leg2
  N1: Part1.GPIO2, S1.Pin_3, S1.Pin_4
  N2: Part1.USBVCC, Part2.VM
  N3: Part1.GPIO5, Part2.AIN2
  N4: Part1.GPIO4, Part2.AIN1
  N5: Part1.GPIO13, Part2.PWMA
  N6: Part1.ADC, R1.wiper
  N7: Part2.A02, M1.pin_1
  N8: Part2.A01, M1.pin_2
