# Fritzing sketch Control_Servo (saved by Fritzing 0.9.3b)
breadboards: 1

parts:
  R1 = Rotary Potentiometer (Small) [maximum_resistance=100kΩ package=THT]
  U1 = NodeMCU V1.0
  J1 = Basic Servo

nets:
  3V3: R1.leg1, U1.3V3, J1.vcc
  N1: R1.wiper, U1.A0
  GND: R1.leg2, U1.GND, J1.gnd
  N2: U1.D1, J1.pulse

custom parts:
  NodeMCU V1.0: ESP8266 based NodeMCU
