# Fritzing sketch 14_Sensor_temperatura_analogo (saved by Fritzing 0.9.3b)
breadboards: 1

parts:
  U1 = NodeMCU V1.0
  U2 = TMP36 [package=to-92-kit]
  OLED1 = OLED 128x64 I2C Monochrome Display

nets:
  N1: U1.D1, OLED1.SCK
  N2: U1.D2, OLED1.SDA
  3V3: U1.3V3, U2.VCC, OLED1.VDD
  GND: U1.GND, U2.GND, OLED1.GND
  N3: U1.A0, U2.VOUT

custom parts:
  NodeMCU V1.0: ESP8266 based NodeMCU
