# Fritzing sketch Control_Servo (saved by Fritzing 0.9.3b)
breadboards: 1

parts:
  U1 = NodeMCU V1.0
  J2 = Basic Servo
  J1 = Basic Servo

nets:
  VCC: U1.3V3, J2.vcc, J1.vcc
  GND: U1.GND, J2.gnd, J1.gnd
  N1: U1.D5, J1.pulse
  N2: U1.D6, J2.pulse

custom parts:
  NodeMCU V1.0: ESP8266 based NodeMCU
