# Fritzing sketch Led (saved by Fritzing 0.9.6b)
breadboards: 1

parts:
  LED1 = smd LED [color="Yellow (595nm)" package="0805 [SMD]"]
  R1 = Resistor [tolerance=±5% resistance=330 package="0402 [SMD]"]
  U1 = NodeMCU V1.0

nets:
  N1: LED1.cathode, R1.Pin_1
  N2: LED1.anode, U1.Vin
  N3: R1.Pin_0, U1.D6

custom parts:
  NodeMCU V1.0: ESP8266 based NodeMCU
