# Fritzing sketch DHT22_sensor (saved by Fritzing 0.9.3b)
breadboards: 1

parts:
  RHT1 = Humidity and Temperature Sensor RHT03
  U1 = NodeMCU V1.0

nets (from the schematic view):
  VCC: RHT1.Vcc, U1.3V3
  N1: RHT1.Data-signal, U1.D5
  N2: RHT1.GND_1, U1.GND

custom parts:
  NodeMCU V1.0: ESP8266 based NodeMCU
