# Fritzing sketch Control_Servo-Potenciometro (saved by Fritzing 0.9.6b)
breadboards: 1

parts:
  U1 = NodeMCU V1.0
  J1 = Basic Servo
  R1 = Rotary Potentiometer (Small) [maximum_resistance=100kΩ package=THT]

nets:
  3V3: U1.3V3, J1.vcc, R1.leg2
  GND: U1.GND, J1.gnd, R1.leg1
  N1: U1.D6, J1.pulse
  N2: U1.A0, R1.wiper

custom parts:
  NodeMCU V1.0: ESP8266 based NodeMCU
