# Fritzing sketch Sleep OLED (saved by Fritzing 0.9.6b)
breadboards: 1

parts:
  U1 = NodeMCU V1.0
  OLED1 = OLED 128x64 I2C Monochrome Display

nets:
  N1: U1.D0, U1.RST
  N2: U1.D1, OLED1.SCK
  N3: U1.D2, OLED1.SDA
  3V3: U1.3V3, OLED1.VDD
  GND: U1.GND, OLED1.GND

custom parts:
  NodeMCU V1.0: ESP8266 based NodeMCU
