# Fritzing sketch Sleep OLED Push Button (saved by Fritzing 0.9.6b)
breadboards: 1

parts:
  U1 = NodeMCU V1.0
  OLED1 = OLED 128x64 I2C Monochrome Display
  S1 = Pushbutton [package="[THT]"]
  R1 = Resistor [tolerance=±5% power=0.25 resistance=220 package=THT]

nets:
  N1: U1.D1, OLED1.SCK
  N2: U1.D2, OLED1.SDA
  3V3: U1.3V3, OLED1.VDD, R1.Pin_0
  GND: U1.GND, OLED1.GND, S1.Pin_1, S1.Pin_2
  N3: U1.RST, S1.Pin_3, S1.Pin_4, R1.Pin_1

custom parts:
  NodeMCU V1.0: ESP8266 based NodeMCU
